// Logisim project logisim_bitsplice.circ as structural Verilog: 4 circuits, main circuit bitslice
module bitslice (
  input  A,
  input  B,
  input  C_IN,
  input  S,
  output C_OUT,
  output F
);

  wire nand_1_out, nand_2_out, nand_3_out, nand_4_out, nand_5_out, not_1_out, not_2_out;

  not not_1 (not_1_out, A);
  nand nand_1 (nand_1_out, B, not_1_out);
  nand nand_2 (nand_2_out, not_1_out, C_IN);
  nand nand_3 (nand_3_out, C_IN, B);
  nand nand_4 (nand_4_out, S, A);
  nand nand_5 (nand_5_out, B, not_2_out);
  not not_2 (not_2_out, S);
  nand nand_6 (C_OUT, nand_1_out, nand_2_out, nand_3_out);
  nand nand_7 (F, nand_4_out, nand_5_out);
endmodule

module main (
  input  in_1,
  input  in_2,
  input  in_3,
  input  A__MSB,
  input  in_5,
  input  in_6,
  input  in_7,
  input  B__MSB,
  output out_9,
  output out_10,
  output out_11,
  output out_12
);

  wire bitslice_1_c_out, bitslice_2_c_out, bitslice_3_c_out, bitslice_4_c_out;

  bitslice bitslice_1 (.F(out_9), .S(bitslice_4_c_out), .A(in_1), .B(in_5), .C_OUT(bitslice_1_c_out), .C_IN(1'b0));
  bitslice bitslice_2 (
    .F(out_10), .S(bitslice_4_c_out), .A(in_2), .B(in_6), .C_OUT(bitslice_2_c_out), .C_IN(bitslice_1_c_out));
  bitslice bitslice_3 (
    .F(out_11), .S(bitslice_4_c_out), .A(in_3), .B(in_7), .C_OUT(bitslice_3_c_out), .C_IN(bitslice_2_c_out));
  bitslice bitslice_4 (
    .F(out_12), .S(bitslice_4_c_out), .A(A__MSB), .B(B__MSB), .C_OUT(bitslice_4_c_out),
    .C_IN(bitslice_3_c_out));
endmodule

module bitslice_cmos (
  input  B,
  input  A,
  input  C_IN,
  input  S,
  output C_OUT,
  output F
);

  wire transistor_1_out, transistor_5_out, transistor_8_out, transistor_9_out, transistor_11_out,
       transistor_13_out, transistor_16_out, transistor_17_out, transistor_19_out, transistor_21_out,
       transistor_24_out, transistor_25_out, transistor_28_out, transistor_29_out, transistor_34_out;

  Transistor transistor_1 (.in(1'b1), .out(transistor_1_out), .gate(B));
  Transistor #(.\type ("n"), .gate("br")) transistor_2 (.in(transistor_11_out), .out(transistor_1_out), .gate(B));
  Transistor #(.\type ("n")) transistor_3 (.in(transistor_17_out), .out(C_OUT), .gate(transistor_1_out));
  Transistor #(.gate("br")) transistor_4 (.in(1'b1), .out(C_OUT), .gate(transistor_1_out));
  Transistor transistor_5 (.in(1'b1), .out(transistor_5_out), .gate(B));
  Transistor transistor_6 (.in(1'b1), .out(transistor_5_out), .gate(transistor_13_out));
  Transistor #(.\type ("n"), .gate("br")) transistor_7 (.in(transistor_8_out), .out(transistor_5_out), .gate(B));
  Transistor #(.\type ("n"), .gate("br")) transistor_8 (.in(1'b0), .out(transistor_8_out), .gate(transistor_13_out));
  Transistor transistor_9 (.in(1'b1), .out(transistor_9_out), .gate(C_IN));
  Transistor transistor_10 (.in(1'b1), .out(transistor_1_out), .gate(C_IN));
  Transistor #(.\type ("n"), .gate("br")) transistor_11 (.in(1'b0), .out(transistor_11_out), .gate(C_IN));
  Transistor #(.\type ("n"), .gate("br")) transistor_12 (.in(transistor_16_out), .out(transistor_9_out), .gate(C_IN));
  Transistor transistor_13 (.in(1'b1), .out(transistor_13_out), .gate(S));
  Transistor #(.\type ("n"), .gate("br")) transistor_14 (.in(1'b0), .out(transistor_13_out), .gate(S));
  Transistor transistor_15 (.in(1'b1), .out(transistor_9_out), .gate(transistor_21_out));
  Transistor #(.\type ("n"), .gate("br")) transistor_16 (.in(1'b0), .out(transistor_16_out), .gate(transistor_21_out));
  Transistor #(.\type ("n")) transistor_17 (.in(transistor_29_out), .out(transistor_17_out), .gate(transistor_9_out));
  Transistor #(.gate("br")) transistor_18 (.in(1'b1), .out(C_OUT), .gate(transistor_9_out));
  Transistor transistor_19 (.in(1'b1), .out(transistor_19_out), .gate(S));
  Transistor #(.\type ("n"), .gate("br")) transistor_20 (.in(transistor_24_out), .out(transistor_19_out), .gate(S));
  Transistor transistor_21 (.in(1'b1), .out(transistor_21_out), .gate(A));
  Transistor #(.\type ("n"), .gate("br")) transistor_22 (.in(1'b0), .out(transistor_21_out), .gate(A));
  Transistor transistor_23 (.in(1'b1), .out(transistor_19_out), .gate(A));
  Transistor #(.\type ("n"), .gate("br")) transistor_24 (.in(1'b0), .out(transistor_24_out), .gate(A));
  Transistor transistor_25 (.in(1'b1), .out(transistor_25_out), .gate(transistor_21_out));
  Transistor transistor_26 (.in(1'b1), .out(transistor_25_out), .gate(B));
  Transistor #(.\type ("n"), .gate("br")) transistor_27 (
    .in(transistor_28_out), .out(transistor_25_out), .gate(transistor_21_out));
  Transistor #(.\type ("n"), .gate("br")) transistor_28 (.in(1'b0), .out(transistor_28_out), .gate(B));
  Transistor #(.\type ("n")) transistor_29 (.in(1'b0), .out(transistor_29_out), .gate(transistor_25_out));
  Transistor #(.gate("br")) transistor_30 (.in(1'b1), .out(C_OUT), .gate(transistor_25_out));
  Transistor transistor_31 (.in(1'b1), .out(F), .gate(transistor_5_out));
  Transistor transistor_32 (.in(1'b1), .out(F), .gate(transistor_19_out));
  Transistor #(.\type ("n"), .gate("br")) transistor_33 (.in(transistor_34_out), .out(F), .gate(transistor_19_out));
  Transistor #(.\type ("n"), .gate("br")) transistor_34 (.in(1'b0), .out(transistor_34_out), .gate(transistor_5_out));
endmodule

module main_cmos (
  input  in_1,
  input  in_2,
  input  in_3,
  input  A__MSB,
  input  in_5,
  input  in_6,
  input  in_7,
  input  B__MSB,
  output out_9,
  output out_10,
  output out_11,
  output out_12
);

  wire bitslice_cmos_1_c_out, bitslice_cmos_2_c_out, bitslice_cmos_3_c_out, bitslice_cmos_4_c_out;

  bitslice_cmos bitslice_cmos_1 (
    .C_IN(1'b0), .C_OUT(bitslice_cmos_1_c_out), .S(bitslice_cmos_4_c_out), .B(in_5), .A(in_1), .F(out_9));
  bitslice_cmos bitslice_cmos_2 (
    .C_IN(bitslice_cmos_1_c_out), .C_OUT(bitslice_cmos_2_c_out), .S(bitslice_cmos_4_c_out), .B(in_6),
    .A(in_2), .F(out_10));
  bitslice_cmos bitslice_cmos_3 (
    .C_IN(bitslice_cmos_2_c_out), .C_OUT(bitslice_cmos_3_c_out), .S(bitslice_cmos_4_c_out), .B(in_7),
    .A(in_3), .F(out_11));
  bitslice_cmos bitslice_cmos_4 (
    .C_IN(bitslice_cmos_3_c_out), .C_OUT(bitslice_cmos_4_c_out), .S(bitslice_cmos_4_c_out), .B(B__MSB),
    .A(A__MSB), .F(out_12));
endmodule
