// Logisim project logisim.circ as structural Verilog: 4 circuits, main circuit carry_slice
module carry_slice (
  input  G,
  input  P,
  input  CI,
  output CO
);

  wire nand_1_out, not_1_out;

  not not_1 (not_1_out, G);
  nand nand_1 (nand_1_out, P, CI);
  nand nand_2 (CO, not_1_out, nand_1_out);
endmodule

module adder_slice (
  input  CI,
  input  A,
  input  B,
  output S,
  output G,
  output P
);

  and and_1 (G, A, B);
  or or_1 (P, A, B);
  Adder #(.width(1)) adder_1 (.a(A), .b(B), .out(S), .cin(CI));  // open: cout
endmodule

module top (
  input  B3,
  input  B2,
  input  B1,
  input  B0,
  input  A3,
  input  A2,
  input  A1,
  input  A0,
  output S3,
  output S2,
  output S1,
  output S0
);

  wire adder_slice_1_g, adder_slice_1_p, adder_slice_2_g, adder_slice_2_p, adder_slice_3_g, adder_slice_3_p,
       adder_slice_4_g, adder_slice_4_p, carry_slice_2_co, carry_slice_3_co, carry_slice_4_co;

  adder_slice adder_slice_1 (.A(A3), .B(B3), .S(S3), .CI(carry_slice_2_co), .G(adder_slice_1_g), .P(adder_slice_1_p));
  carry_slice carry_slice_1 (.G(adder_slice_1_g), .P(adder_slice_1_p), .CI(carry_slice_2_co));  // open: CO
  adder_slice adder_slice_2 (.A(A2), .B(B2), .S(S2), .CI(carry_slice_4_co), .G(adder_slice_2_g), .P(adder_slice_2_p));
  carry_slice carry_slice_2 (.G(adder_slice_2_g), .P(adder_slice_2_p), .CI(carry_slice_4_co), .CO(carry_slice_2_co));
  adder_slice adder_slice_3 (.A(A1), .B(B1), .S(S1), .CI(carry_slice_3_co), .G(adder_slice_3_g), .P(adder_slice_3_p));
  adder_slice adder_slice_4 (.A(A0), .B(B0), .S(S0), .CI(1'b0), .G(adder_slice_4_g), .P(adder_slice_4_p));
  carry_slice carry_slice_3 (.G(adder_slice_4_g), .P(adder_slice_4_p), .CI(1'b0), .CO(carry_slice_3_co));
  carry_slice carry_slice_4 (.G(adder_slice_3_g), .P(adder_slice_3_p), .CI(carry_slice_3_co), .CO(carry_slice_4_co));
endmodule

module carry_slice_fets (
  input  nCLK,
  input  CLK,
  input  P,
  input  G,
  input  CI,
  input  CO
);

  wire transistor_1_out, transistor_3_out, transistor_4_out, transistor_5_out, transistor_6_out;

  Transistor transistor_1 (.in(nCLK), .out(transistor_1_out), .gate(CLK));
  Transistor #(.\type ("n")) transistor_2 (.in(transistor_3_out), .out(transistor_1_out), .gate(P));
  Transistor #(.\type ("n")) transistor_3 (.in(transistor_4_out), .out(transistor_3_out), .gate(CI));
  Transistor #(.\type ("n")) transistor_4 (.in(1'b0), .out(transistor_4_out), .gate(CLK));
  Transistor transistor_5 (.in(1'b1), .out(transistor_5_out), .gate(nCLK));
  Transistor transistor_6 (.in(nCLK), .out(transistor_6_out), .gate(G));
  Transistor #(.\type ("n")) transistor_7 (.in(1'b0), .out(transistor_6_out), .gate(G));
  Transistor transistor_8 (.in(transistor_5_out), .out(CO), .gate(transistor_6_out));
  Transistor #(.gate("br")) transistor_9 (.in(transistor_5_out), .out(CO), .gate(transistor_1_out));
  Transistor #(.\type ("n")) transistor_10 (.in(1'b0), .out(CO), .gate(nCLK));
  // also tied to VCC on the sheet: nCLK
endmodule
