// Logisim project circuit.circ as structural Verilog: 8 circuits, main circuit pin_slice
module pin_slice (
  input  zi,
  input  ci,
  input  qi,
  input  wi,
  output wo,
  output co,
  output qo,
  output zo
);

  wire and_1_out;

  D_Flip_Flop d_ff_1 (.clk(ci), .D(qi), .Q(qo));  // open: Qn, preset, en, reset
  or or_1 (zo, zi, and_1_out);
  and and_1 (and_1_out, qo, wi);

  assign co = ci;
  assign wo = wi;
endmodule

module pin (
  input  PSI,
  input  W0,
  input  W1,
  input  W2,
  input  PCLK,
  output Z0,
  output PSO,
  output PCLKO,
  output Z1,
  output Z2
);

  wire pin_slice_1_co, pin_slice_1_qo, pin_slice_1_zo, pin_slice_2_co, pin_slice_2_qo, pin_slice_2_wo,
       pin_slice_2_zo, pin_slice_3_co, pin_slice_3_qo, pin_slice_3_wo, pin_slice_3_zo, pin_slice_4_co,
       pin_slice_4_qo, pin_slice_4_zo, pin_slice_6_co, pin_slice_6_qo, pin_slice_6_wo, pin_slice_6_zo,
       pin_slice_7_co, pin_slice_7_qo, pin_slice_7_wo, pin_slice_8_co, pin_slice_8_qo, pin_slice_8_wo,
       pin_slice_9_co, pin_slice_9_qo, pin_slice_9_wo, pin_slice_9_zo;

  pin_slice pin_slice_1 (
    .ci(pin_slice_7_co), .qi(pin_slice_7_qo), .zo(pin_slice_1_zo), .wi(pin_slice_2_wo), .zi(1'b0),
    .co(pin_slice_1_co), .qo(pin_slice_1_qo));  // open: wo
  pin_slice pin_slice_2 (
    .ci(pin_slice_8_co), .qi(pin_slice_8_qo), .zo(pin_slice_2_zo), .wi(pin_slice_3_wo), .zi(1'b0),
    .co(pin_slice_2_co), .qo(pin_slice_2_qo), .wo(pin_slice_2_wo));
  pin_slice pin_slice_3 (
    .ci(PCLK), .qi(PSI), .zo(pin_slice_3_zo), .wi(W0), .zi(1'b0), .co(pin_slice_3_co), .qo(pin_slice_3_qo),
    .wo(pin_slice_3_wo));
  pin_slice pin_slice_4 (
    .ci(pin_slice_1_co), .qi(pin_slice_1_qo), .zo(pin_slice_4_zo), .wi(pin_slice_6_wo), .zi(pin_slice_1_zo),
    .co(pin_slice_4_co), .qo(pin_slice_4_qo));  // open: wo
  pin_slice pin_slice_5 (
    .ci(pin_slice_4_co), .qi(pin_slice_4_qo), .zo(Z0), .wi(pin_slice_7_wo), .zi(pin_slice_4_zo), .co(PCLKO),
    .qo(PSO));  // open: wo
  pin_slice pin_slice_6 (
    .ci(pin_slice_2_co), .qi(pin_slice_2_qo), .zo(pin_slice_6_zo), .wi(pin_slice_9_wo), .zi(pin_slice_2_zo),
    .co(pin_slice_6_co), .qo(pin_slice_6_qo), .wo(pin_slice_6_wo));
  pin_slice pin_slice_7 (
    .ci(pin_slice_6_co), .qi(pin_slice_6_qo), .zo(Z1), .wi(pin_slice_8_wo), .zi(pin_slice_6_zo),
    .co(pin_slice_7_co), .qo(pin_slice_7_qo), .wo(pin_slice_7_wo));
  pin_slice pin_slice_8 (
    .ci(pin_slice_9_co), .qi(pin_slice_9_qo), .zo(Z2), .wi(W2), .zi(pin_slice_9_zo), .co(pin_slice_8_co),
    .qo(pin_slice_8_qo), .wo(pin_slice_8_wo));
  pin_slice pin_slice_9 (
    .ci(pin_slice_3_co), .qi(pin_slice_3_qo), .zo(pin_slice_9_zo), .wi(W1), .zi(pin_slice_3_zo),
    .co(pin_slice_9_co), .qo(pin_slice_9_qo), .wo(pin_slice_9_wo));
endmodule

module shift (
  input  SI,
  input  SCLKI,
  input  LDI,
  input  Z0,
  input  Z1,
  input  Z2,
  output W0,
  output W1,
  output W2,
  output SO,
  output SCLKO,
  output LDO
);

  wire shift_slice_1_ldo, shift_slice_1_sclko, shift_slice_2_ldo, shift_slice_2_sclko;

  shift_slice shift_slice_1 (
    .SCLKI(SCLKI), .LDI(LDI), .Z(Z0), .SI(SI), .SCLKO(shift_slice_1_sclko), .LDO(shift_slice_1_ldo), .SO(W0));
  shift_slice shift_slice_2 (
    .SCLKI(shift_slice_1_sclko), .LDI(shift_slice_1_ldo), .Z(Z1), .SI(W0), .SCLKO(shift_slice_2_sclko),
    .LDO(shift_slice_2_ldo), .SO(W1));
  shift_slice shift_slice_3 (
    .SCLKI(shift_slice_2_sclko), .LDI(shift_slice_2_ldo), .Z(Z2), .SI(W1), .SCLKO(SCLKO), .LDO(LDO), .SO(SO));

  assign W2 = SO;
endmodule

module top_internal (
  input  PSI,
  input  SI,
  input  LDI,
  output PSO,
  output PCLKO,
  output SO,
  output SCLKO,
  output LDO
);

  wire PCLKI_out, pin_slice_1_co, pin_slice_1_qo, pin_slice_1_zo, pin_slice_2_co, pin_slice_2_qo,
       pin_slice_2_wo, pin_slice_2_zo, pin_slice_3_co, pin_slice_3_qo, pin_slice_3_wo, pin_slice_3_zo,
       pin_slice_4_co, pin_slice_4_qo, pin_slice_4_zo, pin_slice_5_co, pin_slice_5_qo, pin_slice_5_wo,
       pin_slice_5_zo, pin_slice_6_co, pin_slice_6_qo, pin_slice_6_wo, pin_slice_6_zo, pin_slice_7_zo,
       pin_slice_8_co, pin_slice_8_qo, pin_slice_8_wo, pin_slice_8_zo, pin_slice_9_co, pin_slice_9_qo,
       pin_slice_9_wo, pin_slice_9_zo, SCLKI_out, shift_slice_1_ldo, shift_slice_1_sclko, shift_slice_1_so,
       shift_slice_2_ldo, shift_slice_2_sclko, shift_slice_2_so;

  Button PCLKI (.out(PCLKI_out));
  Button SCLKI (.out(SCLKI_out));
  pin_slice pin_slice_1 (
    .ci(pin_slice_8_co), .qi(pin_slice_8_qo), .zo(pin_slice_1_zo), .wi(pin_slice_2_wo), .zi(1'b0),
    .co(pin_slice_1_co), .qo(pin_slice_1_qo));  // open: wo
  pin_slice pin_slice_2 (
    .ci(pin_slice_9_co), .qi(pin_slice_9_qo), .zo(pin_slice_2_zo), .wi(pin_slice_3_wo), .zi(1'b0),
    .co(pin_slice_2_co), .qo(pin_slice_2_qo), .wo(pin_slice_2_wo));
  pin_slice pin_slice_3 (
    .ci(PCLKI_out), .qi(PSI), .zo(pin_slice_3_zo), .wi(shift_slice_1_so), .zi(1'b0), .co(pin_slice_3_co),
    .qo(pin_slice_3_qo), .wo(pin_slice_3_wo));
  shift_slice shift_slice_1 (
    .SCLKI(SCLKI_out), .LDI(LDI), .Z(pin_slice_7_zo), .SI(SI), .SCLKO(shift_slice_1_sclko),
    .LDO(shift_slice_1_ldo), .SO(shift_slice_1_so));
  pin_slice pin_slice_4 (
    .ci(pin_slice_1_co), .qi(pin_slice_1_qo), .zo(pin_slice_4_zo), .wi(pin_slice_5_wo), .zi(pin_slice_1_zo),
    .co(pin_slice_4_co), .qo(pin_slice_4_qo));  // open: wo
  pin_slice pin_slice_5 (
    .ci(pin_slice_2_co), .qi(pin_slice_2_qo), .zo(pin_slice_5_zo), .wi(pin_slice_6_wo), .zi(pin_slice_2_zo),
    .co(pin_slice_5_co), .qo(pin_slice_5_qo), .wo(pin_slice_5_wo));
  pin_slice pin_slice_6 (
    .ci(pin_slice_3_co), .qi(pin_slice_3_qo), .zo(pin_slice_6_zo), .wi(shift_slice_2_so),
    .zi(pin_slice_3_zo), .co(pin_slice_6_co), .qo(pin_slice_6_qo), .wo(pin_slice_6_wo));
  shift_slice shift_slice_2 (
    .SCLKI(shift_slice_1_sclko), .LDI(shift_slice_1_ldo), .Z(pin_slice_8_zo), .SI(shift_slice_1_so),
    .SCLKO(shift_slice_2_sclko), .LDO(shift_slice_2_ldo), .SO(shift_slice_2_so));
  pin_slice pin_slice_7 (
    .ci(pin_slice_4_co), .qi(pin_slice_4_qo), .zo(pin_slice_7_zo), .wi(pin_slice_8_wo), .zi(pin_slice_4_zo),
    .co(PCLKO), .qo(PSO));  // open: wo
  pin_slice pin_slice_8 (
    .ci(pin_slice_5_co), .qi(pin_slice_5_qo), .zo(pin_slice_8_zo), .wi(pin_slice_9_wo), .zi(pin_slice_5_zo),
    .co(pin_slice_8_co), .qo(pin_slice_8_qo), .wo(pin_slice_8_wo));
  pin_slice pin_slice_9 (
    .ci(pin_slice_6_co), .qi(pin_slice_6_qo), .zo(pin_slice_9_zo), .wi(SO), .zi(pin_slice_6_zo),
    .co(pin_slice_9_co), .qo(pin_slice_9_qo), .wo(pin_slice_9_wo));
  shift_slice shift_slice_3 (
    .SCLKI(shift_slice_2_sclko), .LDI(shift_slice_2_ldo), .Z(pin_slice_9_zo), .SI(shift_slice_2_so),
    .SCLKO(SCLKO), .LDO(LDO), .SO(SO));
endmodule

module shift_slice (
  input  SCLKI,
  input  LDI,
  input  SI,
  input  Z,
  output SCLKO,
  output LDO,
  output SO
);

  wire multiplexer_1_out;

  Multiplexer #(.disabled(0), .enable("false")) multiplexer_1 (.in0(SI), .in1(Z), .out(multiplexer_1_out), .sel(LDI));
  D_Flip_Flop d_ff_1 (.clk(SCLKI), .D(multiplexer_1_out), .Q(SO));  // open: Qn, preset, en, reset

  assign LDO = LDI;
  assign SCLKO = SCLKI;
endmodule

module top (
  input  PSI,
  input  PCLKI,
  input  SI,
  input  SCLKI,
  input  LDI,
  output PSO,
  output PCLKO,
  output SO,
  output SCLKO,
  output LDO
);

  wire pin_1_z0, pin_1_z1, pin_1_z2, shift_1_w0, shift_1_w1, shift_1_w2;

  shift shift_1 (
    .SI(SI), .SCLKI(SCLKI), .LDI(LDI), .SO(SO), .W0(shift_1_w0), .W1(shift_1_w1), .W2(shift_1_w2),
    .Z0(pin_1_z0), .Z1(pin_1_z1), .Z2(pin_1_z2), .SCLKO(SCLKO), .LDO(LDO));
  pin pin_1 (
    .PSI(PSI), .PCLK(PCLKI), .Z0(pin_1_z0), .Z1(pin_1_z1), .Z2(pin_1_z2), .W0(shift_1_w0), .W1(shift_1_w1),
    .W2(shift_1_w2), .PSO(PSO), .PCLKO(PCLKO));
endmodule

module test_mode (
  input  PSI,
  input  PCLKI,
  input  TESTI,
  input  SI,
  input  SCLKI,
  input  LDI,
  output PSO,
  output PCLKO,
  output TESTO,
  output SO,
  output SCLKO,
  output LDO
);

  wire multiplexer_1_out, multiplexer_2_out, pin_1_z0, pin_1_z1, pin_1_z2, shift_1_so, shift_1_w0,
       shift_1_w1, shift_1_w2;

  Multiplexer #(.enable("false")) multiplexer_1 (.in0(PSI), .in1(shift_1_so), .out(multiplexer_1_out), .sel(TESTI));
  Multiplexer #(.enable("false")) multiplexer_2 (.in0(PCLKI), .in1(SCLKO), .out(multiplexer_2_out), .sel(TESTI));
  shift shift_1 (
    .SI(SI), .SCLKI(SCLKI), .LDI(LDI), .SO(shift_1_so), .W0(shift_1_w0), .W1(shift_1_w1), .W2(shift_1_w2),
    .Z0(pin_1_z0), .Z1(pin_1_z1), .Z2(pin_1_z2), .SCLKO(SCLKO), .LDO(LDO));
  pin pin_1 (
    .PSI(multiplexer_1_out), .PCLK(multiplexer_2_out), .Z0(pin_1_z0), .Z1(pin_1_z1), .Z2(pin_1_z2),
    .W0(shift_1_w0), .W1(shift_1_w1), .W2(shift_1_w2), .PSO(PSO), .PCLKO(PCLKO));
  Multiplexer #(.enable("false")) multiplexer_3 (.in0(shift_1_so), .in1(PSO), .out(SO), .sel(TESTI));

  assign TESTO = TESTI;
endmodule

module chain (
  input  PSI,
  input  PCLK,
  input  TESTI,
  input  SI,
  input  SCLK,
  input  LD,
  output TESTO,
  output SO
);

  wire test_mode_1_ldo, test_mode_1_pclko, test_mode_1_pso, test_mode_1_sclko, test_mode_1_so,
       test_mode_1_testo, test_mode_2_ldo, test_mode_2_pclko, test_mode_2_pso, test_mode_2_sclko,
       test_mode_2_so, test_mode_2_testo;

  test_mode test_mode_1 (
    .PSI(PSI), .PCLKI(PCLK), .TESTI(TESTI), .SI(SI), .SCLKI(SCLK), .LDI(LD), .PSO(test_mode_1_pso),
    .PCLKO(test_mode_1_pclko), .TESTO(test_mode_1_testo), .SO(test_mode_1_so), .SCLKO(test_mode_1_sclko),
    .LDO(test_mode_1_ldo));
  test_mode test_mode_2 (
    .PSI(test_mode_1_pso), .PCLKI(test_mode_1_pclko), .TESTI(test_mode_1_testo), .SI(test_mode_1_so),
    .SCLKI(test_mode_1_sclko), .LDI(test_mode_1_ldo), .PSO(test_mode_2_pso), .PCLKO(test_mode_2_pclko),
    .TESTO(test_mode_2_testo), .SO(test_mode_2_so), .SCLKO(test_mode_2_sclko), .LDO(test_mode_2_ldo));
  test_mode test_mode_3 (
    .PSI(test_mode_2_pso), .PCLKI(test_mode_2_pclko), .TESTI(test_mode_2_testo), .SI(test_mode_2_so),
    .SCLKI(test_mode_2_sclko), .LDI(test_mode_2_ldo), .TESTO(TESTO), .SO(SO));  // open: PSO, PCLKO, SCLKO, LDO
endmodule
