// Logisim project dynamic_gates.circ as structural Verilog: 5 circuits, main circuit n_nor
module n_nor (
);

  wire transistor_1_out, transistor_4_out;

  Transistor transistor_1 (.in(1'b1), .out(transistor_1_out));  // open: gate
  Transistor #(.\type ("n"), .gate("br")) transistor_2 (.in(transistor_4_out), .out(transistor_1_out));  // open: gate
  Transistor #(.\type ("n")) transistor_3 (.in(transistor_4_out), .out(transistor_1_out));  // open: gate
  Transistor #(.\type ("n")) transistor_4 (.in(1'b0), .out(transistor_4_out));  // open: gate

  // Notes on the sheet:
  //   CLK
  //   A
  //   CLK
  //   F
  //   B
endmodule

module p_nor (
);

  wire transistor_1_out, transistor_2_out, transistor_3_out;

  Transistor transistor_1 (.in(1'b1), .out(transistor_1_out));  // open: gate
  Transistor transistor_2 (.in(transistor_1_out), .out(transistor_2_out));  // open: gate
  Transistor transistor_3 (.in(transistor_2_out), .out(transistor_3_out));  // open: gate
  Transistor #(.\type ("n")) transistor_4 (.in(1'b0), .out(transistor_3_out));  // open: gate

  // Notes on the sheet:
  //   CLK
  //   A
  //   B
  //   F
  //   CLK
endmodule

module n_nand (
);

  wire transistor_1_out, transistor_3_out, transistor_4_out;

  Transistor transistor_1 (.in(1'b1), .out(transistor_1_out));  // open: gate
  Transistor #(.\type ("n")) transistor_2 (.in(transistor_3_out), .out(transistor_1_out));  // open: gate
  Transistor #(.\type ("n")) transistor_3 (.in(transistor_4_out), .out(transistor_3_out));  // open: gate
  Transistor #(.\type ("n")) transistor_4 (.in(1'b0), .out(transistor_4_out));  // open: gate

  // Notes on the sheet:
  //   CLK
  //   F
  //   A
  //   B
  //   CLK
endmodule

module p_nand (
);

  wire transistor_1_out, transistor_2_out;

  Transistor transistor_1 (.in(1'b1), .out(transistor_1_out));  // open: gate
  Transistor transistor_2 (.in(transistor_1_out), .out(transistor_2_out));  // open: gate
  Transistor #(.gate("br")) transistor_3 (.in(transistor_1_out), .out(transistor_2_out));  // open: gate
  Transistor #(.\type ("n")) transistor_4 (.in(1'b0), .out(transistor_2_out));  // open: gate

  // Notes on the sheet:
  //   CLK
  //   A
  //   CLK
  //   B
  //   F
endmodule

module all (
);

  wire transistor_1_out, transistor_4_out, transistor_5_out, transistor_6_out, transistor_7_out,
       transistor_9_out, transistor_11_out, transistor_12_out, transistor_13_out, transistor_14_out;

  Transistor transistor_1 (.in(1'b1), .out(transistor_1_out));  // open: gate
  Transistor #(.\type ("n"), .gate("br")) transistor_2 (.in(transistor_4_out), .out(transistor_1_out));  // open: gate
  Transistor #(.\type ("n")) transistor_3 (.in(transistor_4_out), .out(transistor_1_out));  // open: gate
  Transistor #(.\type ("n")) transistor_4 (.in(1'b0), .out(transistor_4_out));  // open: gate
  Transistor transistor_5 (.in(1'b1), .out(transistor_5_out));  // open: gate
  Transistor transistor_6 (.in(transistor_5_out), .out(transistor_6_out));  // open: gate
  Transistor transistor_7 (.in(transistor_6_out), .out(transistor_7_out));  // open: gate
  Transistor #(.\type ("n")) transistor_8 (.in(1'b0), .out(transistor_7_out));  // open: gate
  Transistor transistor_9 (.in(1'b1), .out(transistor_9_out));  // open: gate
  Transistor #(.\type ("n")) transistor_10 (.in(transistor_11_out), .out(transistor_9_out));  // open: gate
  Transistor #(.\type ("n")) transistor_11 (.in(transistor_12_out), .out(transistor_11_out));  // open: gate
  Transistor #(.\type ("n")) transistor_12 (.in(1'b0), .out(transistor_12_out));  // open: gate
  Transistor transistor_13 (.in(1'b1), .out(transistor_13_out));  // open: gate
  Transistor transistor_14 (.in(transistor_13_out), .out(transistor_14_out));  // open: gate
  Transistor #(.gate("br")) transistor_15 (.in(transistor_13_out), .out(transistor_14_out));  // open: gate
  Transistor #(.\type ("n")) transistor_16 (.in(1'b0), .out(transistor_14_out));  // open: gate

  // Notes on the sheet:
  //   A
  //   CLK
  //   F
  //   B
  //   CLK
  //   N NOR
  //   CLK
  //   A
  //   B
  //   F
  //   CLK
  //   P NOR
  //   CLK
  //   F
  //   CLK
  //   A
  //   B
  //   A
  //   CLK
  //   CLK
  //   N NAND
  //   B
  //   F
  //   P NAND
endmodule
